# Fritzing sketch New_Radio (saved by Fritzing 0.9.3b)

parts:
  Part1 = Adafruit Music Maker Shield no Amp [part_number="Adafruit #1790"]
  Part2 = Arduino Uno (Rev3) - ICSP
  Part3 = Adafruit MAX9744 20W Amplifier [part_number="Adafruit #1752"]
  U1 = RELAY [package=relay-jzc]  # not connected
  U2 = AUDIO-JACK2 [package=audio-jack]  # not connected
  U3 = AUDIO-JACK2 [package=audio-jack]  # not connected

nets:
  N1: Part1.SD_CS, Part2.D4
  N2: Part1.DREQ, Part2.D3_PWM
  N3: Part1.MP3_CS, Part2.D7
  N4: Part1.XDCS, Part2.D6_PWM
  N5: Part1.MISO_ICSP, Part2.D12/MISO
  N6: Part1.MOSI_ICSP, Part2.D11_PWM/MOSI
  N7: Part1.SCK_ICSP, Part2.D13/SCK
  N8: Part2.A5/SCL, Part3.SCL
  N9: Part2.5V, Part3.VI2C
  N10: Part2.ICSP_MOSI, Part3.SDA
  GND: Part2.GND, Part3.GND

custom parts:
  Adafruit Music Maker Shield no Amp: Bend all audio files to your will with the Adafruit Music Maker shield for Arduino! This powerful shield features the VS1053, an encoding/decoding (codec) chip that can decode a wide variety of audio formats such as MP3, AAC, Ogg Vorbis, WMA, MIDI, FLAC, WAV (PCM and ADPCM). It can also be used to record audio in both PCM (WAV) and compressed Ogg Vorbis. You can do all sorts of stuff with the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
  Adafruit MAX9744 20W Amplifier: Pump up the volume with this 20W stereo amplifier! This slim little board has a class D amplifier onboard that can drive 2 channels of 4-8 ohm impedance speakers at 20W each. Power it with 5-12VDC using the onboard DC power jack and plug stereo line level into the 3.5mm stereo headphone jack and jam out with ease. Since it's class D, its completely cool-running, no heat sinks are required and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
