# Fritzing sketch Organized_board (saved by Fritzing 0.9.3b)
stripboards: 1

parts:
  TRS1 = Audio Jack (TRS) 3.5mm [package="4Ucon 08780 [THT]"]
  TRS2 = Audio Jack (TRS) 3.5mm [package="4Ucon 08780 [THT]"]
  J1 = Camdenboss CTB0158-3 [part_number=CTB0158-3 package=THT]
  R1 = Resistor [tolerance=±5% resistance=1k package=THT]
  R2 = Resistor [tolerance=±5% resistance=1k package=THT]
  R3 = Resistor [tolerance=±5% resistance=100k package=THT]
  R4 = Resistor [tolerance=±5% resistance=100k package=THT]

nets:
  N1: TRS1.Sleeve, J1.terminal_3, R3.Pin_0, R4.Pin_0
  N2: TRS1.Ring, TRS2.Ring, J1.terminal_2
  N3: TRS1.Tip, TRS2.Sleeve, TRS2.Tip, J1.terminal_1, R1.Pin_0, R2.Pin_0, R3.Pin_1, R4.Pin_1
  N4: R1.Pin_1, R2.Pin_1

notes:
  GPIO2
  D2
  D5
