# Fritzing sketch OG_Breadboard_Schematic (saved by Fritzing 0.9.3b)
stripboards: 1

parts:
  R1 = Resistor [tolerance=±5% resistance=100k package=THT]
  TRS1 = Audio Jack (TRS) 3.5mm [package="PG203J [THT]"]
  R2 = Resistor [tolerance=±5% resistance=1k package="0402 [SMD]"]
  R3 = Resistor [tolerance=±5% resistance=1k package="0402 [SMD]"]
  R4 = Resistor [tolerance=±5% resistance=100k package=THT]
  Part1 = Adafruit Music Maker Shield with Amp [part_number="Adafruit #1788"]
  U1 = RELAY [package=relay-jzc]
  Part2 = Arduino Uno (Rev3) - ICSP
  TRS2 = Audio Jack (TRS) 3.5mm [package="PG203J [THT]"]

nets:
  N1: R1.Pin_0, TRS1.Sleeve, R4.Pin_0, U1.NC, Part2.GND, TRS2.Sleeve
  N2: R1.Pin_1, TRS1.Tip, R2.Pin_0, R3.Pin_0, R4.Pin_1, Part1.GPIO2, Part1.D5, TRS2.Tip
  N3: TRS1.Ring, TRS2.Ring
  N4: R2.Pin_1, R3.Pin_1, U1.NO, Part2.3V3
  N5: Part1.D2, U1.COIL2

custom parts:
  Adafruit Music Maker Shield with Amp: Bend all audio files to your will with the Adafruit Music Maker shield for Arduino! This powerful shield features the VS1053, an encoding/decoding (codec) chip that can decode a wide variety of audio formats such as MP3, AAC, Ogg Vorbis, WMA, MIDI, FLAC, WAV (PCM and ADPCM). It can also be used to record audio in both PCM (WAV) and compressed Ogg Vorbis. You can do all sorts of stuff with the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
