# Fritzing sketch Radio_Schematic (saved by Fritzing 0.9.3b)
breadboards: 1
stripboards: 1

parts:
  Part1 = Arduino Uno (Rev3)
  Part2 = Adafruit VS1053 Headphone FeatherWing [part_number="Adafruit #3357"]
  Part3 = Adafruit MAX9744 20W Amplifier [part_number="Adafruit #1752"]
  U1 = RELAY [package=relay-jzc]  # not connected
  SP1 = SPEAKER [package=pcb_mount_speaker]  # not connected
  U2 = POT [package=pot_mammoth]  # not connected
  U3 = POT [package=pot_mammoth]  # not connected

nets:
  N1: Part1.A4/SDA, Part3.SDA
  N2: Part1.A5/SCL, Part3.SCL
  N3: Part1.D9_PWM, Part2.!RESET
  N4: Part1.D11_PWM/MOSI, Part2.MOSI
  N5: Part1.D12/MISO, Part2.MISO
  N6: Part1.D13/SCK, Part2.SCLK
  GND: Part1.GND, Part2.GND, Part3.GND
  N7: Part1.D3_PWM, Part2.DREQ
  N8: Part1.D5_PWM, Part2.SD_CS
  N9: Part1.D6_PWM, Part2.MP3CS
  N10: Part1.D7, Part2.XDCS
  3V3: Part1.3V3, Part2.3.3V
  N11: Part1.5V, Part3.VI2C
  N12: Part2.LEFT_OUT, Part3.LEFTIN
  N13: Part2.AGND, Part3.AGND

custom parts:
  Adafruit VS1053 Headphone FeatherWing: Bend all audio files to your will with the Adafruit Music Maker FeatherWing! It's a fun-size version of our Music Maker shield for Arduino! This powerful shield features the VS1053, an encoding/decoding (codec) chip that can decode a wide variety of audio formats such as MP3, AAC, Ogg Vorbis, WMA, MIDI, FLAC, WAV (PCM and ADPCM). You can do all sorts of stuff with the audio as well such as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
  Adafruit MAX9744 20W Amplifier: Pump up the volume with this 20W stereo amplifier! This slim little board has a class D amplifier onboard that can drive 2 channels of 4-8 ohm impedance speakers at 20W each. Power it with 5-12VDC using the onboard DC power jack and plug stereo line level into the 3.5mm stereo headphone jack and jam out with ease. Since it's class D, its completely cool-running, no heat sinks are required and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
